// Logisim project ipc.circ as structural Verilog: 2 circuits, main circuit main
module main (
);

  wire acz, adc, add, add_out, adder_1_cout, amov, and_2_out, and_3_out, and_4_out, and_5_out, and_6_out,
       and_8_out, and_9_out, and_10_out, and_11_out, and_12_out, and_13_out, and_14_out, and_15_out,
       and_16_out, and_17_out, and_18_out, and_19_out, and_20_out, and_21_out, and_22_out, and_23_out,
       and_24_out, and_25_out, and_26_out, and_27_out, and_28_out, and_29_out, and_30_out, and_31_out, bca,
       bnc, bnz, bpa, bsi, button_1_out, button_2_out, button_3_out, button_4_out, button_5_out,
       button_6_out, bze, carryt, clc, clock_1_out, clockt, ctrl_alu, ctrl_reg_in, ctrl_reg_out,
       ctrl_setting_carry, ctrl_sub, ctrl_using_adder, cur_byte_im, decoder_2_out0, decoder_2_out1,
       decoder_2_out2, decoder_2_out3, decoder_2_out4, decoder_2_out5, decoder_2_out6, decoder_2_out7, hlt,
       i_and, i_in, i_nor, i_out, i_ror, i_xor, im_to_reg, ima, imr, jmp, ld, nop, nor_2_out, nor_3_out,
       nor_4_out, nor_5_out, not_1_out, not_2_out, not_3_out, or_1_out, or_2_out, or_3_out, or_4_out,
       parityt, pop, push, rmov, sbc, signt, spc, stc, str, sub, undriven, undriven_2, xor_1_out, xor_10_out,
       zerot;
  wire [0:0] ram_1_data_2;
  wire [2:0] multiplexer_1_out, register_1_q;
  wire [6:0] ram_1_data;
  wire [7:0] ac, adder_1_out, and_7_out, bph, bpl, controlled_buffer_1_out, inputd, mah, mal, marh, marl,
       multiplexer_2_out, nor_1_out, opcode, out_d, prog_out, r0, r1, r2, r3, r4, sf, sp, sph, spl, xor_2_out;
  wire [15:0] counter_1_q;

  and and_1 (clockt, ~hlt, clock_1_out);  // AND_Gate
  Counter #(.max('hffff), .trigger("falling"), .width(16)) counter_1 (
    .load(undriven), .D({marh, marl}), .count(1'b1), .Q(counter_1_q), .up(1'b1), .clk(clockt));  // open: carry, clr
  Clock clock_1 (.out(clock_1_out));
  ROM #(.addrWidth(16)) rom_1 (.addr(counter_1_q), .data(prog_out));
  RAM #(.addrWidth(16), .databus("bidir"), .enables("line")) ram_1 (
    .addr({marh, marl}), .data({ram_1_data, ram_1_data_2[0]}));  // open: we, oe, clk
  not not_1 (not_1_out, cur_byte_im);
  Decoder #(.select(5)) decoder_1 (
    .out0(add), .out1(sub), .out2(adc), .out3(sbc), .out4(i_ror), .out5(i_nor), .out6(i_and), .out7(i_xor),
    .out9(stc), .out10(clc), .out11(rmov), .out12(amov), .out13(jmp), .out14(bca), .out15(bnc), .out16(bze),
    .out17(bnz), .out18(bsi), .out19(bpa), .out20(acz), .out21(ima), .out22(imr), .out23(spc), .out24(str),
    .out25(ld), .out26(i_in), .out27(i_out), .out28(nop), .out29(hlt), .out30(push), .out31(pop),
    .sel(prog_out[4:0]), .en(not_1_out));  // open: out8
  or using_adder (ctrl_using_adder, add_out, ctrl_sub);
  or u_add (add_out, add, adc);
  or or_1 (or_1_out, ima, imr);
  or register_out (ctrl_reg_out, ctrl_alu, rmov, str, push, i_out);
  or alu (ctrl_alu, ctrl_setting_carry, i_ror, i_nor, i_and);
  or setting_carry (ctrl_setting_carry, ctrl_using_adder, i_ror);
  or u_sub (ctrl_sub, sub, sbc);
  D_Flip_Flop #(.trigger("falling")) d_ff_1 (.D(and_2_out), .clk(clockt), .Q(cur_byte_im));  // open: Qn, preset, reset
  and and_2 (and_2_out, or_1_out, ~cur_byte_im);  // AND_Gate
  or register_in (ctrl_reg_in, and_3_out, amov, i_in, ld, pop);
  and and_3 (and_3_out, im_to_reg, cur_byte_im);
  Pull_Resistor pull_resistor_1 (.node({ram_1_data, ram_1_data_2[0]}));
  and and_4 (and_4_out, carryt, sbc);
  Register #(.width(4)) register_1 (
    .D({imr, prog_out[7:5]}), .en(1'b1), .clk(clockt), .Q({im_to_reg, register_1_q}));  // open: clr
  xor xor_1 (xor_1_out, and_4_out, ctrl_sub);
  xor xor_2 (xor_2_out[0], ram_1_data_2[0], ctrl_sub);
  xor xor_3 (xor_2_out[1], ram_1_data[0], ctrl_sub);
  Multiplexer #(.width(3)) multiplexer_1 (
    .in0(prog_out[7:5]), .in1(register_1_q), .out(multiplexer_1_out), .sel(cur_byte_im));
  and and_5 (and_5_out, adc, carryt);
  or or_2 (or_2_out, and_5_out, and_6_out);
  and and_6 (and_6_out, xor_1_out, ctrl_sub);
  Adder adder_1 (.a(ac), .b(xor_2_out), .out(adder_1_out), .cin(or_2_out), .cout(adder_1_cout));
  xor xor_4 (xor_2_out[2], ram_1_data[1], ctrl_sub);
  xor xor_5 (xor_2_out[3], ram_1_data[2], ctrl_sub);
  assign nor_1_out = ~({ram_1_data, ram_1_data_2[0]} | ac);  // NOR_Gate nor_1, 8 bits wide
  assign and_7_out = {ram_1_data, ram_1_data_2[0]} & ac;  // AND_Gate and_7, 8 bits wide
  Decoder #(.enable("false"), .select(3)) decoder_2 (
    .out0(decoder_2_out0), .out1(decoder_2_out1), .out2(decoder_2_out2), .out3(decoder_2_out3),
    .out4(decoder_2_out4), .out5(decoder_2_out5), .out6(decoder_2_out6), .out7(decoder_2_out7),
    .sel(multiplexer_1_out));
  assign controlled_buffer_1_out = ctrl_using_adder ? adder_1_out : 8'bz;  // Controlled_Buffer controlled_buffer_1
  xor xor_6 (xor_2_out[4], ram_1_data[3], ctrl_sub);
  xor xor_7 (xor_2_out[5], ram_1_data[4], ctrl_sub);
  assign controlled_buffer_1_out = i_ror ? {carryt, ram_1_data} : 8'bz;  // Controlled_Buffer controlled_buffer_2
  assign controlled_buffer_1_out = i_nor ? nor_1_out : 8'bz;  // Controlled_Buffer controlled_buffer_3
  assign controlled_buffer_1_out = i_and ? and_7_out : 8'bz;  // Controlled_Buffer controlled_buffer_4
  xor xor_8 (xor_2_out[6], ram_1_data[5], ctrl_sub);
  xor xor_9 (xor_2_out[7], ram_1_data[6], ctrl_sub);
  xor xor_10 (xor_10_out, adder_1_cout, ctrl_sub);
  not not_2 (not_2_out, ctrl_using_adder);
  nor nor_2 (nor_2_out, controlled_buffer_1_out[7], controlled_buffer_1_out[6]);
  nor nor_3 (nor_3_out, controlled_buffer_1_out[5], controlled_buffer_1_out[4]);
  and and_8 (and_8_out, nor_2_out, nor_3_out);
  assign {ram_1_data, ram_1_data_2[0]} = cur_byte_im ? prog_out : 8'bz;  // Controlled_Buffer controlled_buffer_5
  and and_9 (and_9_out, xor_10_out, ctrl_using_adder);
  or or_3 (or_3_out, and_9_out, and_10_out);
  and and_10 (and_10_out, ram_1_data_2[0], not_2_out);
  nor nor_4 (nor_4_out, controlled_buffer_1_out[3], controlled_buffer_1_out[2]);
  nor nor_5 (nor_5_out, controlled_buffer_1_out[1], controlled_buffer_1_out[0]);
  and and_11 (and_11_out, nor_4_out, nor_5_out);
  and and_12 (and_12_out, and_8_out, and_11_out);
  and and_13 (and_13_out, ctrl_alu, clockt);
  assign out_d = i_out ? {ram_1_data, ram_1_data_2[0]} : 8'bz;  // Controlled_Buffer controlled_buffer_6
  and and_14 (and_14_out, decoder_2_out7, ctrl_reg_out);
  and and_15 (and_15_out, ctrl_reg_in, decoder_2_out7);
  and and_16 (and_16_out, decoder_2_out6, ctrl_reg_out);
  and and_17 (and_17_out, ctrl_reg_in, decoder_2_out6);
  and and_18 (and_18_out, decoder_2_out5, ctrl_reg_out);
  and and_19 (and_19_out, ctrl_reg_in, decoder_2_out5);
  and and_20 (and_20_out, decoder_2_out4, ctrl_reg_out);
  and and_21 (and_21_out, ctrl_reg_in, decoder_2_out4);
  and and_22 (and_22_out, decoder_2_out3, ctrl_reg_out);
  and and_23 (and_23_out, ctrl_reg_in, decoder_2_out3);
  and and_24 (and_24_out, decoder_2_out2, ctrl_reg_out);
  and and_25 (and_25_out, ctrl_reg_in, decoder_2_out2);
  and and_26 (and_26_out, decoder_2_out1, ctrl_reg_out);
  and and_27 (and_27_out, ctrl_reg_in, decoder_2_out1);
  and and_28 (and_28_out, decoder_2_out0, ctrl_reg_out);
  and and_29 (and_29_out, decoder_2_out0, ctrl_reg_in);
  Multiplexer #(.width(8)) multiplexer_2 (
    .in0({ram_1_data, ram_1_data_2[0]}), .in1(controlled_buffer_1_out), .out(multiplexer_2_out),
    .sel(ctrl_alu));
  or or_4 (or_4_out, ctrl_alu, and_30_out, rmov);
  and and_30 (and_30_out, not_3_out, cur_byte_im);
  not not_3 (not_3_out, im_to_reg);
  Pull_Resistor pull_resistor_2 (.node(controlled_buffer_1_out));
  Register u_marh (.D({ram_1_data, ram_1_data_2[0]}), .en(and_15_out), .clk(clockt), .Q(marh));  // open: clr
  Register u_marl (.D({ram_1_data, ram_1_data_2[0]}), .en(and_17_out), .clk(clockt), .Q(marl));  // open: clr
  Register u_sph (.D({ram_1_data, ram_1_data_2[0]}), .en(and_19_out), .clk(clockt), .Q(sph));  // open: clr
  Register u_spl (.D({ram_1_data, ram_1_data_2[0]}), .en(and_21_out), .clk(clockt), .Q(spl));  // open: clr
  Register u_bph (.D({ram_1_data, ram_1_data_2[0]}), .en(and_23_out), .clk(clockt), .Q(bph));  // open: clr
  Register u_bpl (.D({ram_1_data, ram_1_data_2[0]}), .en(and_25_out), .clk(clockt), .Q(bpl));  // open: clr
  Register u_r1 (.D({ram_1_data, ram_1_data_2[0]}), .en(and_27_out), .clk(clockt), .Q(r1));  // open: clr
  Register u_r0 (.D({ram_1_data, ram_1_data_2[0]}), .en(and_29_out), .clk(clockt), .Q(r0));  // open: clr
  Register u_ac (.D(multiplexer_2_out), .en(or_4_out), .clk(clockt), .Q(ac));  // open: clr
  D_Flip_Flop carryf (.D(or_3_out), .clk(and_31_out), .Q(carryt), .preset(clc), .reset(stc));  // open: Qn
  and and_31 (and_31_out, ctrl_setting_carry, clockt);
  D_Flip_Flop zerof (.D(and_12_out), .clk(and_13_out), .Q(zerot));  // open: Qn, preset, reset
  D_Flip_Flop signf (.D(controlled_buffer_1_out[7]), .clk(and_13_out), .Q(signt));  // open: Qn, preset, reset
  D_Flip_Flop parityf (.D(controlled_buffer_1_out[0]), .clk(and_13_out), .Q(parityt));  // open: Qn, preset, reset
  assign {ram_1_data, ram_1_data_2[0]} = i_in ? inputd : 8'bz;  // Controlled_Buffer controlled_buffer_7
  assign {ram_1_data, ram_1_data_2[0]} = and_14_out ? marh : 8'bz;  // Controlled_Buffer controlled_buffer_8
  assign {ram_1_data, ram_1_data_2[0]} = and_16_out ? marl : 8'bz;  // Controlled_Buffer controlled_buffer_9
  assign {ram_1_data, ram_1_data_2[0]} = and_18_out ? sph : 8'bz;  // Controlled_Buffer controlled_buffer_10
  assign {ram_1_data, ram_1_data_2[0]} = and_20_out ? spl : 8'bz;  // Controlled_Buffer controlled_buffer_11
  assign {ram_1_data, ram_1_data_2[0]} = and_22_out ? bph : 8'bz;  // Controlled_Buffer controlled_buffer_12
  assign {ram_1_data, ram_1_data_2[0]} = and_24_out ? bpl : 8'bz;  // Controlled_Buffer controlled_buffer_13
  assign {ram_1_data, ram_1_data_2[0]} = and_26_out ? r1 : 8'bz;  // Controlled_Buffer controlled_buffer_14
  assign {ram_1_data, ram_1_data_2[0]} = and_28_out ? r0 : 8'bz;  // Controlled_Buffer controlled_buffer_15
  assign {ram_1_data, ram_1_data_2[0]} = amov ? ac : 8'bz;  // Controlled_Buffer controlled_buffer_16
  // Probe on r1
  // Probe on sp
  // Probe on opcode
  input_cont input_cont_1 (
    .in_0(button_1_out), .in_1(button_3_out), .in_2(button_2_out), .in_3(button_4_out), .in_4(button_5_out),
    .in_sig(i_in), .in_5(button_6_out), .clock_input(clockt), .input_data(inputd));
  Button button_1 (.out(button_1_out));
  Button button_2 (.out(button_2_out));
  Button button_3 (.out(button_3_out));
  Button button_4 (.out(button_4_out));
  // Probe on r2
  // Probe on sf
  // Probe on ac
  Button button_5 (.out(button_5_out));
  // Probe on r3
  // Probe on mal
  LED led_1 (.in(undriven_2));
  Button button_6 (.out(button_6_out));
  // Probe on r4
  // Probe on mah

  // Notes on the sheet:
  //   contents of rom_1 (hex, n*v repeats v):
  //   1a 1e f6 0 d6 0 10 b6 4 ab 6 f6 0 d6 30 11 b6 8 ab 6 f6 0 d6 3a 11 b6 1 ab 6 f6 0 d6 44 11 b6 2 ab 6
  //   f6 0 d6 4c 11 f6 0 d6 0 d b6 1 ab 20 2c f6 0 d6 0 d b6 1 2b a1 2c f6 0 d6 0 d 2b 20 2c f6 0 d6 0 d a
  //   24 2c f6 0 d6 0 d
  //   A
  //   B
  //   ROR
  //   Carry is set by Adder or ROR
endmodule

module input_cont (
  input  in_sig,
  input  clock_input,
  input  in_0,
  input  in_1,
  input  in_2,
  input  in_3,
  input  in_4,
  input  in_5,
  output [7:0] input_data
);

  wire and_1_out, or_1_out;
  wire [7:0] multiplexer_1_out, or_2_out, pull_resistor_1_node, pull_resistor_3_node, register_1_q;
  wire [7:6] pull_resistor_2_node;

  or or_1 (or_1_out, in_0, in_1, in_2, in_3, in_4, in_5);
  Pull_Resistor pull_resistor_1 (.node(pull_resistor_1_node));
  assign or_2_out = {pull_resistor_2_node, in_5, in_4, in_3, in_2, in_1, in_0} | register_1_q;  // OR_Gate or_2, 8 bits wide
  Pull_Resistor pull_resistor_2 (.node({pull_resistor_2_node, in_5, in_4, in_3, in_2, in_1, in_0}));
  and and_1 (and_1_out, ~or_1_out, in_sig);  // AND_Gate
  Register #(.trigger("falling")) register_1 (
    .D(multiplexer_1_out), .en(1'b1), .clk(clock_input), .Q(register_1_q));  // open: clr
  Multiplexer #(.width(8)) multiplexer_1 (
    .in0(or_2_out), .in1(pull_resistor_1_node), .out(multiplexer_1_out));  // open: sel
  Pull_Resistor pull_resistor_3 (.node(pull_resistor_3_node));
  // Probe on register_1_q
  Multiplexer #(.width(8)) multiplexer_2 (
    .in0(pull_resistor_3_node), .in1(register_1_q), .out(input_data));  // open: sel
endmodule
